// Logisim project rudimentary computing device.circ as structural Verilog: 1 circuit, main circuit main
module main (
  input  [5:0] in_1,
  input  [5:0] in_2,
  input  [5:0] in_3,
  input  in_4,
  input  in_5,
  input  in_6,
  input  in_7,
  input  in_8,
  input  in_9,
  output [5:0] out_10,
  output [5:0] out_11,
  output [5:0] out_12
);

  wire button_1_out, clock_1_out, main_2_add, main_2_insert, main_2_out;
  wire [5:0] main_1_out_14, main_4_out_19, main_5_out_18, main_6_out_18, main_7_out_18, main_8_out_8,
       main_8_out_9, main_8_out_10, main_9_out_8, main_9_out_9, main_9_out_10;
  wire [18:0] rom_1_data;

  Clock clock_1 (.out(clock_1_out));
  LED led_1 (.in(main_1_out_14[5]));
  LED led_2 (.in(main_1_out_14[4]));
  Button button_1 (.out(button_1_out));
  LED led_3 (.in(main_1_out_14[1]));
  LED led_4 (.in(main_1_out_14[0]));
  LED led_5 (.in(main_1_out_14[3]));
  LED led_6 (.in(main_1_out_14[2]));
  program_counter_main main_1 (
    .in_7(button_1_out), .in_8(clock_1_out), .out_9(main_1_out_14[5]), .out_10(main_1_out_14[4]),
    .out_11(main_1_out_14[3]), .out_12(main_1_out_14[2]), .out_13(main_1_out_14[1]),
    .out_14(main_1_out_14[0]), .in_1(in_4), .in_2(in_5), .in_3(in_6), .in_4(in_7), .in_5(in_8), .in_6(in_9));
  instructor_main main_2 (
    .in_1(rom_1_data[18]), .in_2(rom_1_data[17]), .in_3(rom_1_data[16]), .in_4(rom_1_data[15]),
    .ADD(main_2_add), .INSERT(main_2_insert), .OUT(main_2_out));  // open: INVERT, A_B, A_B_2, A_B_3, STEP, HALT, out_14, out_15, out_16
  input_selector_main main_3 (
    .in_4(main_2_out), .in_1({6{1'b0}}), .in_2({6{1'b0}}), .in_3({6{1'b0}}), .in_5(main_5_out_18),
    .in_6(main_6_out_18), .in_7(main_7_out_18), .out_8(out_10), .out_9(out_11), .out_10(out_12));
  addition_main main_4 (
    .in_1(main_6_out_18[5]), .in_2(main_6_out_18[4]), .in_3(main_6_out_18[3]), .in_4(main_6_out_18[2]),
    .in_5(main_6_out_18[1]), .in_6(main_6_out_18[0]), .in_7(main_5_out_18[5]), .in_8(main_5_out_18[4]),
    .in_9(main_5_out_18[3]), .in_10(main_5_out_18[2]), .in_11(main_5_out_18[1]), .in_12(main_5_out_18[0]),
    .out_14(main_4_out_19[5]), .out_15(main_4_out_19[4]), .out_16(main_4_out_19[3]),
    .out_17(main_4_out_19[2]), .out_18(main_4_out_19[1]), .out_19(main_4_out_19[0]));  // open: out_13
  ROM #(.addrWidth(6), .dataWidth(19)) rom_1 (.addr(main_1_out_14), .data(rom_1_data));  // open: sel
  memory_main main_5 (
    .Address(rom_1_data[14]), .in_2(rom_1_data[13]), .Write(rom_1_data[12]), .in_4(rom_1_data[11]),
    .Read(rom_1_data[10]), .Initialise(button_1_out), .in_7(main_9_out_8[5]), .in_8(main_9_out_8[4]),
    .Input(main_9_out_8[3]), .in_10(main_9_out_8[2]), .in_11(main_9_out_8[1]), .in_12(main_9_out_8[0]),
    .out_13(main_5_out_18[5]), .out_14(main_5_out_18[4]), .Output(main_5_out_18[3]),
    .out_16(main_5_out_18[2]), .out_17(main_5_out_18[1]), .out_18(main_5_out_18[0]));
  memory_main main_6 (
    .Address(rom_1_data[9]), .in_2(rom_1_data[8]), .Write(rom_1_data[7]), .in_4(rom_1_data[6]),
    .Read(rom_1_data[5]), .Initialise(button_1_out), .in_7(main_9_out_9[5]), .in_8(main_9_out_9[4]),
    .Input(main_9_out_9[3]), .in_10(main_9_out_9[2]), .in_11(main_9_out_9[1]), .in_12(main_9_out_9[0]),
    .out_13(main_6_out_18[5]), .out_14(main_6_out_18[4]), .Output(main_6_out_18[3]),
    .out_16(main_6_out_18[2]), .out_17(main_6_out_18[1]), .out_18(main_6_out_18[0]));
  memory_main main_7 (
    .Address(rom_1_data[4]), .in_2(rom_1_data[3]), .Write(rom_1_data[2]), .in_4(rom_1_data[1]),
    .Read(rom_1_data[0]), .Initialise(button_1_out), .in_7(main_9_out_10[5]), .in_8(main_9_out_10[4]),
    .Input(main_9_out_10[3]), .in_10(main_9_out_10[2]), .in_11(main_9_out_10[1]), .in_12(main_9_out_10[0]),
    .out_13(main_7_out_18[5]), .out_14(main_7_out_18[4]), .Output(main_7_out_18[3]),
    .out_16(main_7_out_18[2]), .out_17(main_7_out_18[1]), .out_18(main_7_out_18[0]));
  input_selector_main main_8 (
    .in_4(main_2_insert), .in_1({6{1'b0}}), .in_2({6{1'b0}}), .in_3({6{1'b0}}), .in_5(in_1), .in_6(in_2),
    .in_7(in_3), .out_8(main_8_out_8), .out_9(main_8_out_9), .out_10(main_8_out_10));
  input_selector_main main_9 (
    .in_4(main_2_add), .in_1(main_8_out_8), .in_2(main_8_out_9), .in_3(main_8_out_10), .in_5({6{1'b0}}),
    .in_6({6{1'b0}}), .in_7(main_4_out_19), .out_8(main_9_out_8), .out_9(main_9_out_9), .out_10(main_9_out_10));

  // Notes on the sheet:
  //   contents of rom_1 (hex, n*v repeats v):
  //   39800 380c0 94a6 40005 40000 6 7 8 9 a b c d e f
endmodule
